# Fritzing sketch circuit (saved by Fritzing 0.9.3b)
breadboards: 1

parts:
  Часть1 = Arduino Uno (Rev3)
  R2 = Trimmer Potentiometer [maximum_resistance=10kΩ package=THT]
  J1 = Basic Servo

nets:
  N1: Часть1.A0, R2.wiper
  N2: Часть1.D9_PWM, J1.pulse
  5V: Часть1.5V, R2.leg2, J1.vcc
  GND: Часть1.GND, R2.leg1, J1.gnd
