# Fritzing sketch circuit (saved by Fritzing 0.9.3b)
breadboards: 1

parts:
  Часть1 = Arduino Uno (Rev3)
  LCD1 = LCD screen
  R1 = Trimmer Potentiometer [maximum_resistance=10kΩ package=THT]
  U1 = TMP36 [package=to-92-kit]

nets:
  N1: Часть1.A1, U1.VOUT
  N2: Часть1.D8, LCD1.E
  N3: Часть1.D3_PWM, LCD1.DB4
  N4: Часть1.D4, LCD1.DB5
  N5: Часть1.D5_PWM, LCD1.DB6
  N6: Часть1.D6_PWM, LCD1.DB7
  N7: Часть1.D7, LCD1.RS
  5V: Часть1.5V, LCD1.VDD, LCD1.LED+, R1.leg1, U1.VCC
  GND: Часть1.GND, LCD1.VSS, LCD1.R/W, LCD1.LED-, R1.leg2, U1.GND
  N8: LCD1.V0, R1.wiper
